# Fritzing sketch Sketch (saved by Fritzing 0.9.3b)
breadboards: 1

parts:
  Raspberry_Pi_1 = Raspberry Pi 3 [part_number=RPI-3-V1.2]
  IC1 = MCP3008 8-channel 10-bit ADC [part_number=MCP3008]
  Part1 = Soil Moisture Sensor
  U1 = 4-Channel 5v Relay Shield [package=relay-4ch5v10a]
  Power_plug1 = Power plug
  M1 = DC Motor
  M2 = DC Motor
  M3 = DC Motor
  M4 = DC Motor

nets:
  N1: Raspberry_Pi_1.3v3, IC1.no_name_yet#15, IC1.no_name_yet#16
  N2: Raspberry_Pi_1.GPIO4, U1.IN4
  N3: Raspberry_Pi_1.GPIO17, U1.IN3
  N4: Raspberry_Pi_1.GPIO27, U1.IN2
  N5: Raspberry_Pi_1.GPIO22, U1.IN1
  N6: Raspberry_Pi_1.GPIO10, IC1.no_name_yet#11
  N7: Raspberry_Pi_1.GPIO9, IC1.no_name_yet#12
  N8: Raspberry_Pi_1.GPIO11, IC1.no_name_yet#13
  GND: Raspberry_Pi_1.GND, IC1.no_name_yet#9, IC1.no_name_yet#14, Part1.GND, U1.GND
  N9: Raspberry_Pi_1.GPIO21, Part1.VCC
  N10: Raspberry_Pi_1.GPIO8, IC1.no_name_yet#10
  5V: Raspberry_Pi_1.5V, U1.VCC
  N11: IC1.no_name_yet#1, Part1.SIG
  N12: U1.K1-Off, M4.pin_1
  N13: U1.K1-On, U1.K2-On, U1.K3-On, U1.K4-On, Power_plug1.VCC
  N14: U1.K2-Off, M3.pin_1
  N15: U1.K3-Off, M2.pin_1
  N16: U1.K4-Off, M1.pin_1
  N17: Power_plug1.GND, M1.pin_2, M2.pin_2, M3.pin_2, M4.pin_2

notes:
  12V water pump

custom parts:
  4-Channel 5v Relay Shield: 4 Channel 5v Relay Shield w. 2x SPD-06VDC-SD-C
