# Fritzing sketch Arduino_Prototyp_01_fritz (saved by Fritzing 0.9.2b)
breadboards: 1

parts:
  WeMos_D1_Mini1 = WeMos D1 Mini  # not connected
  WeMos_D1_Mini_Battery_Shield1 = WeMos D1 Mini Battery Shield
  WeMos_D1_Mini2 = WeMos D1 Mini  # not connected
  U1 = LIPO-2000mAh [package=lipo-2000]  # not connected
  S1 = Pushbutton [package="[THT]"]
  PART1 = SparkFun Soil Moisture Sensor [part_number=SEN-13322]

nets:
  3V3: WeMos_D1_Mini_Battery_Shield1.3V3, PART1.VCC
  N1: WeMos_D1_Mini_Battery_Shield1.A0, PART1.SIG
  N2: WeMos_D1_Mini_Battery_Shield1.D3, S1.Pin_1, S1.Pin_2
  N3: WeMos_D1_Mini_Battery_Shield1.G, S1.Pin_3, S1.Pin_4, PART1.GND

custom parts:
  SparkFun Soil Moisture Sensor: The SparkFun Soil Moisture Sensor is a simple breakout for measuring the moisture in soil and similar materials.
